# Fritzing sketch led-toggle (saved by Fritzing 0.9.0b)
circuit board: 6cm x 3cm
breadboards: 1

parts:
  LED1 = LEDs [package=led10mm]
  LED2 = LEDs [package=led10mm]
  BAT1 = Battery Holders [package=battcom_20mm_pth]
  U1 = 555 Timer [package="DIP8 [THT]"]
  C1 = Electrolytic Capacitor [capacitance=10μF package="200 mil [THT, electrolytic]"]
  R2 = Resistor [tolerance=±5% resistance=220 package=THT]
  R3 = Resistor [tolerance=±5% resistance=220 package=THT]
  R4 = Resistor [tolerance=±5% resistance=220 package=THT]
  R1 = Resistor [tolerance=±5% resistance=220 package=THT]

nets:
  N1: LED1.A, R2.Pin_0
  N2: LED1.C, U1.Output, R3.Pin_1
  N3: LED2.A, R3.Pin_0
  N4: LED2.C, BAT1.-, U1.Ground, C1.-
  N5: BAT1.+, U1.Reset, U1.Vcc_Supply_Voltage, R2.Pin_1, R1.Pin_0
  N6: U1.Trigger, U1.Threshold, C1.+, R4.Pin_0
  N7: U1.Discharge, R4.Pin_1, R1.Pin_1
